// Logisim project Basic Computer Circuit.circ as structural Verilog: 33 circuits, main circuit main
module main (
  input  [7:0] \input ,
  output [7:0] \output 
);

  wire ac_control_1_clear, ac_control_1_increment, add, ALU_load, \and , ar_control_1_clear,
       ar_control_1_incremnt, ar_control_1_load, B0, B1, B2, B3, B4, B5, B6, B7, B8, B9, B10, B11, clock,
       clock_out, comp, D0, D1, D2, D3, D4, D5, D6, D7, dr_control_1_increment, dr_control_1_load, DR_load,
       E, e_control_1_clear, e_control_1_complement, e_control_1_load, E_in, FGI, FGO, I, I_in, IEN,
       inpr_load, ir_control_1_load, not_1_out, outr_control_1_load, p, pc_control_1_clear,
       pc_control_1_increment, pc_control_1_load, R, r_t, ram_control_1_load, ram_control_1_store,
       sc_control_1_sc_clear, shl, shr, T0, T1, T2, T3, T4, T5, T6, T7, T8, T9, T10, T11, T12, T13, T14, T15,
       tr_control_1_load;
  wire [3:0] sc_1_sc_out;
  wire [7:0] INPR;
  wire [11:0] RAM_address;
  wire [15:0] AC, ALU, AR, BUS_OUT, DR, IR, PC, RAM, TR;

  E_control e_control_1 (
    .load(e_control_1_load), .complement(e_control_1_complement), .clear(e_control_1_clear), .r(r_t),
    .T5(T5), .D1(D1), .B6(B6), .B7(B7), .B8(B8), .B10(B10));
  AC_control ac_control_1 (
    .load(ALU_load), .increment(ac_control_1_increment), .clear(ac_control_1_clear), .r(r_t), .p(p), .T5(T5),
    .D0(D0), .D1(D1), .D2(D2), .B5(B5), .B6(B6), .B7(B7), .B9(B9), .B11(B11), .\and (\and ), .add(add),
    .DR_load(DR_load), .INPR_load(inpr_load), .shr(shr), .shl(shl), .complement(comp));
  not not_1 (not_1_out, I);
  and and_1 (r_t, not_1_out, T3, D7);
  and and_2 (p, T3, I, D7);
  R r_1 (.R(R), .T0(T0), .T1(T1), .T2(T2), .FGI(FGI), .FGO(FGO), .IEN(IEN), .clock(clock));
  FGO fgo_1 (.FGO(FGO), .p(p), .B10(B10), .T0(T0), .clock(clock));
  BUS bus_1 (
    .AR(AR), .PC(PC), .DR(DR), .AC(AC), .IR(IR), .TR(TR), .RAM(RAM), .BUS_OUT(BUS_OUT), .I(I), .R(R),
    .T0(T0), .T1(T1), .T2(T2), .T3(T3), .T4(T4), .T5(T5), .T6(T6), .D0(D0), .D1(D1), .D2(D2), .D3(D3),
    .D4(D4), .D5(D5), .D6(D6), .D7(D7), .p(p), .B10(B10));
  I i_1 (.I(I), .I_in(I_in), .R(R), .T2(T2), .clock(clock));
  IEN ien_1 (.IEN(IEN), .p(p), .R(R), .T2(T2), .B6(B6), .B7(B7), .clock(clock));
  FGI fgi_1 (.FGI(FGI), .p(p), .B11(B11), .INPR(INPR), .clock(clock));
  E e_1 (
    .E_input(E_in), .complement(e_control_1_complement), .E_output(E), .clock(clock),
    .load(e_control_1_load), .clear(e_control_1_clear));
  AC ac_1 (
    .BUS_in(ALU), .increment(ac_control_1_increment), .load(ALU_load), .clear(ac_control_1_clear),
    .BUS_out(AC), .clock(clock));
  TR_control tr_control_1 (.R(R), .T0(T0), .load(tr_control_1_load));
  OUTR_control outr_control_1 (.p(p), .B10(B10), .load(outr_control_1_load));
  Hex_Digit_Display hex_digit_display_1 (.value(AC[15:12]));  // open: dp
  Hex_Digit_Display hex_digit_display_2 (.value(AC[11:8]));  // open: dp
  TR tr_1 (.BUS_in(BUS_OUT), .load(tr_control_1_load), .BUS_out(TR), .clock(clock));  // open: clear
  OUTR outr_1 (.out(\output ), .load(outr_control_1_load), .clock(clock), .BUS_in(BUS_OUT));
  INPR inpr_1 (.\input (\input ), .\output (INPR), .clock(clock));
  Hex_Digit_Display hex_digit_display_3 (.value(AC[3:0]));  // open: dp
  Hex_Digit_Display hex_digit_display_4 (.value(AC[7:4]));  // open: dp
  PC_control pc_control_1 (
    .increment(pc_control_1_increment), .load(pc_control_1_load), .clear(pc_control_1_clear), .R(R),
    .r_2(r_t), .p(p), .E(E), .FGI(FGI), .FGO(FGO), .T1(T1), .T2(T2), .T4(T4), .T5(T5), .T6(T6), .D4(D4),
    .D5(D5), .D6(D6), .B1(B1), .B2(B2), .B3(B3), .B4(B4), .B8(B8), .B9(B9), .AC(AC), .DR(DR));
  AR_control ar_control_1 (
    .INCREMNT(ar_control_1_incremnt), .LOAD(ar_control_1_load), .CLEAR(ar_control_1_clear), .I(I), .R(R),
    .T0(T0), .T2(T2), .T3(T3), .T4(T4), .D5(D5), .D7(D7));
  DR_control dr_control_1 (
    .load(dr_control_1_load), .increment(dr_control_1_increment), .T4(T4), .T5(T5), .D0(D0), .D1(D1),
    .D2(D2), .D6(D6));
  RAM_Control ram_control_1 (
    .store(ram_control_1_store), .load(ram_control_1_load), .I(I), .R(R), .T1(T1), .T3(T3), .T4(T4), .T6(T6),
    .D0(D0), .D1(D1), .D2(D2), .D3(D3), .D5(D5), .D6(D6), .D7(D7));
  IR_control ir_control_1 (.R(R), .T1(T1), .load(ir_control_1_load));
  Hex_Digit_Display hex_digit_display_5 (.value(BUS_OUT[15:12]));  // open: dp
  Hex_Digit_Display hex_digit_display_6 (.value(BUS_OUT[11:8]));  // open: dp
  Hex_Digit_Display hex_digit_display_7 (.value(BUS_OUT[7:4]));  // open: dp
  Hex_Digit_Display hex_digit_display_8 (.value(BUS_OUT[3:0]));  // open: dp
  PC pc_1 (
    .BUS_in(BUS_OUT), .BUS_out(PC), .increment(pc_control_1_increment), .load(pc_control_1_load),
    .clear(pc_control_1_clear), .clock(clock));
  IR ir_1 (
    .bus_in(BUS_OUT), .D0(D0), .D1(D1), .D2(D2), .D3(D3), .D4(D4), .D5(D5), .D6(D6), .D7(D7), .bus_out(IR),
    .I(I_in), .load(ir_control_1_load), .clock(clock), .B0(B0), .B1(B1), .B2(B2), .B3(B3), .B4(B4), .B5(B5),
    .B6(B6), .B7(B7), .B8(B8), .B9(B9), .B10(B10), .B11(B11));
  DR dr_1 (
    .BUS_in(BUS_OUT), .increment(dr_control_1_increment), .load(dr_control_1_load), .BUS_out(DR),
    .clock(clock));  // open: clear
  AR ar_1 (
    .BUS_input(BUS_OUT), .inc(ar_control_1_incremnt), .load(ar_control_1_load), .clock(clock),
    .clear(ar_control_1_clear), .RAM_AR(RAM_address), .BUS_out(AR));
  Hex_Digit_Display hex_digit_display_9 (.value(RAM[15:12]));  // open: dp
  RAM #(.addrWidth(12), .dataWidth(16), .bus("separate")) ram_1 (
    .addr(RAM_address), .din(BUS_OUT), .data(RAM), .str(ram_control_1_store), .sel(1'b1), .clk(clock),
    .ld(ram_control_1_load));  // open: clr
  Hex_Digit_Display hex_digit_display_10 (.value(RAM[11:8]));  // open: dp
  Hex_Digit_Display hex_digit_display_11 (.value(RAM[7:4]));  // open: dp
  Hex_Digit_Display hex_digit_display_12 (.value(IR[15:12]));  // open: dp
  Hex_Digit_Display hex_digit_display_13 (.value(RAM[3:0]));  // open: dp
  Hex_Digit_Display hex_digit_display_14 (.value(AR[11:8]));  // open: dp
  Hex_Digit_Display hex_digit_display_15 (.value(AR[15:12]));  // open: dp
  Hex_Digit_Display hex_digit_display_16 (.value(IR[7:4]));  // open: dp
  Hex_Digit_Display hex_digit_display_17 (.value(IR[11:8]));  // open: dp
  Hex_Digit_Display hex_digit_display_18 (.value(PC[11:8]));  // open: dp
  Hex_Digit_Display hex_digit_display_19 (.value(PC[15:12]));  // open: dp
  Hex_Digit_Display hex_digit_display_20 (.value(DR[15:12]));  // open: dp
  Hex_Digit_Display hex_digit_display_21 (.value(DR[11:8]));  // open: dp
  Hex_Digit_Display hex_digit_display_22 (.value(AR[3:0]));  // open: dp
  Hex_Digit_Display hex_digit_display_23 (.value(AR[7:4]));  // open: dp
  Hex_Digit_Display hex_digit_display_24 (.value(IR[3:0]));  // open: dp
  Hex_Digit_Display hex_digit_display_25 (.value(PC[3:0]));  // open: dp
  Hex_Digit_Display hex_digit_display_26 (.value(PC[7:4]));  // open: dp
  Hex_Digit_Display hex_digit_display_27 (.value(DR[7:4]));  // open: dp
  Hex_Digit_Display hex_digit_display_28 (.value(DR[3:0]));  // open: dp
  Hex_Digit_Display hex_digit_display_29 (.value(sc_1_sc_out));  // open: dp
  SC sc_1 (
    .sc_clr(sc_control_1_sc_clear), .sc_clock(clock), .T0(T0), .T1(T1), .T2(T2), .T3(T3), .T4(T4), .T5(T5),
    .T6(T6), .T7(T7), .T8(T8), .T9(T9), .T10(T10), .T11(T11), .T12(T12), .T13(T13), .T14(T14), .T15(T15),
    .SC_out(sc_1_sc_out));
  Clock u_clock (.out(clock_out));
  CLOCK clock_2 (.clock(clock_out), .r(r_t), .B0(B0), .clock_out(clock));
  ALU alu_1 (
    .INPR(INPR), .AC(AC), .DR(DR), .AC_out(ALU), .E(E), .load(ALU_load), .E_out(E_in), .\and (\and ),
    .add(add), .DR_load(DR_load), .INPR_load(inpr_load), .complement(comp), .shr(shr), .shl(shl));
  SC_control sc_control_1 (
    .R(R), .T3(T3), .D6(D6), .I(I), .D0(D0), .D1(D1), .D2(D2), .D5(D5), .T4(T4), .D4(D4), .D3(D3), .T5(T5),
    .T6(T6), .T7(T7), .D7(D7), .SC_clear(sc_control_1_sc_clear));
  Hex_Digit_Display hex_digit_display_30 (.value(ALU[15:12]));  // open: dp
  Hex_Digit_Display hex_digit_display_31 (.value(ALU[7:4]));  // open: dp
  Hex_Digit_Display hex_digit_display_32 (.value(ALU[11:8]));  // open: dp
  Hex_Digit_Display hex_digit_display_33 (.value(ALU[3:0]));  // open: dp
endmodule

module CLOCK (
  input  clock,
  input  r,
  input  B0,
  output clock_out
);

  wire and_1_out, d_ff_1_qn, j_k_ff_1_q;

  and and_1 (and_1_out, r, B0);
  J_K_Flip_Flop j_k_ff_1 (.J(and_1_out), .clk(clock), .K(1'b0), .Q(j_k_ff_1_q));  // open: Qn, preset, en, reset
  D_Flip_Flop d_ff_1 (.clk(clock), .D(j_k_ff_1_q), .Qn(d_ff_1_qn));  // open: Q, preset, en, reset
  and and_2 (clock_out, clock, d_ff_1_qn);
endmodule

module BUS (
  input  I,
  input  R,
  input  T0,
  input  T1,
  input  T2,
  input  T3,
  input  T4,
  input  T5,
  input  T6,
  input  D0,
  input  D1,
  input  D2,
  input  D3,
  input  D4,
  input  D5,
  input  D6,
  input  D7,
  input  p,
  input  B10,
  input  [15:0] AR,
  input  [15:0] PC,
  input  [15:0] DR,
  input  [15:0] AC,
  input  [15:0] IR,
  input  [15:0] TR,
  input  [15:0] RAM,
  output [15:0] BUS_OUT
);

  wire and_1_out, and_2_out, and_3_out, and_4_out, and_5_out, and_6_out, and_7_out, and_8_out, and_9_out,
       and_10_out, and_11_out, and_12_out, and_13_out, decoder_1_out1, decoder_1_out2, decoder_1_out3,
       decoder_1_out4, decoder_1_out5, decoder_1_out6, decoder_1_out7, not_1_out, not_2_out, not_3_out,
       or_1_out, or_2_out, or_3_out, or_4_out, or_5_out, or_6_out;
  wire [2:0] priority_encoder_1_out;

  not not_1 (not_1_out, R);
  and and_1 (and_1_out, T4, D4);
  and and_2 (and_2_out, T5, D5);
  and and_3 (and_3_out, T4, D5);
  and and_4 (and_4_out, T5, D2);
  and and_5 (and_5_out, T6, D6);
  and and_6 (and_6_out, B10, p);
  and and_7 (and_7_out, T4, D3);
  and and_8 (and_8_out, not_1_out, T2);
  and and_9 (and_9_out, R, T1);
  or or_1 (or_1_out, D0, D1, D2, D6);
  not not_2 (not_2_out, D7);
  not not_3 (not_3_out, R);
  and and_10 (and_10_out, not_3_out, T1);
  or or_2 (or_2_out, and_1_out, and_2_out);
  or or_3 (or_3_out, T0, and_3_out);
  or or_4 (or_4_out, and_4_out, and_5_out);
  or or_5 (or_5_out, and_6_out, and_7_out);
  and and_11 (and_11_out, or_1_out, T4);
  and and_12 (and_12_out, not_2_out, I, T3);
  or or_6 (or_6_out, and_11_out, and_12_out, and_10_out);
  and and_13 (and_13_out, ~or_2_out, ~or_3_out, ~or_4_out, ~or_5_out, ~and_8_out, ~and_9_out, ~or_6_out);  // AND_Gate
  Priority_Encoder priority_encoder_1 (
    .in0(and_13_out), .in1(or_2_out), .in2(or_3_out), .in3(or_4_out), .in4(or_5_out), .in5(and_8_out),
    .in6(and_9_out), .in7(or_6_out), .out(priority_encoder_1_out));  // open: en_in, gs, en_out
  Decoder #(.select(3)) decoder_1 (
    .out1(decoder_1_out1), .out2(decoder_1_out2), .out3(decoder_1_out3), .out4(decoder_1_out4),
    .out5(decoder_1_out5), .out6(decoder_1_out6), .out7(decoder_1_out7), .sel(priority_encoder_1_out),
    .en(1'b1));  // open: out0
  assign BUS_OUT = decoder_1_out1 ? AR : 16'bz;  // Controlled_Buffer controlled_buffer_1
  assign BUS_OUT = decoder_1_out2 ? PC : 16'bz;  // Controlled_Buffer controlled_buffer_2
  assign BUS_OUT = decoder_1_out3 ? DR : 16'bz;  // Controlled_Buffer controlled_buffer_3
  assign BUS_OUT = decoder_1_out4 ? AC : 16'bz;  // Controlled_Buffer controlled_buffer_4
  assign BUS_OUT = decoder_1_out5 ? IR : 16'bz;  // Controlled_Buffer controlled_buffer_5
  assign BUS_OUT = decoder_1_out6 ? TR : 16'bz;  // Controlled_Buffer controlled_buffer_6
  assign BUS_OUT = decoder_1_out7 ? RAM : 16'bz;  // Controlled_Buffer controlled_buffer_7
endmodule

module SC (
  input  sc_clr,
  input  sc_clock,
  output T0,
  output T1,
  output T2,
  output T3,
  output T4,
  output T5,
  output T6,
  output T7,
  output T8,
  output T9,
  output T10,
  output T11,
  output T12,
  output T13,
  output T14,
  output T15,
  output [3:0] SC_out
);

  wire not_1_out;

  not not_1 (not_1_out, sc_clr);
  Decoder #(.select(4)) decoder_1 (
    .out0(T0), .out1(T1), .out2(T2), .out3(T3), .out4(T4), .out5(T5), .out6(T6), .out7(T7), .out8(T8),
    .out9(T9), .out10(T10), .out11(T11), .out12(T12), .out13(T13), .out14(T14), .out15(T15), .sel(SC_out));  // open: en
  Counter #(.width(4), .max('hf)) sc (
    .count(not_1_out), .Q(SC_out), .clk(sc_clock), .clr(sc_clr));  // open: load, D, carry
endmodule

module SC_control (
  input  I,
  input  R,
  input  T3,
  input  T4,
  input  T5,
  input  T6,
  input  T7,
  input  D0,
  input  D1,
  input  D2,
  input  D3,
  input  D4,
  input  D5,
  input  D6,
  input  D7,
  output SC_clear
);

  wire and_1_out, and_2_out, and_3_out, and_4_out, and_5_out, and_6_out, or_1_out, or_2_out;

  and and_1 (and_1_out, ~I, T4, D7);  // AND_Gate
  and and_2 (and_2_out, I, T4, D7);
  and and_3 (and_3_out, R, T3);
  or or_1 (or_1_out, D0, D1, D2, D5);
  or or_2 (or_2_out, D3, D4);
  and and_4 (and_4_out, D6, T7);
  and and_5 (and_5_out, or_1_out, T6);
  and and_6 (and_6_out, or_2_out, T5);
  or or_3 (SC_clear, and_1_out, and_2_out, and_3_out, and_5_out, and_6_out, and_4_out);
endmodule

module RAM_Control (
  input  I,
  input  R,
  input  T1,
  input  T3,
  input  T4,
  input  T6,
  input  D0,
  input  D1,
  input  D2,
  input  D3,
  input  D5,
  input  D6,
  input  D7,
  output store,
  output load
);

  wire and_1_out, and_2_out, and_3_out, and_4_out, and_5_out, and_6_out, and_7_out, not_1_out, not_2_out,
       or_1_out;

  and and_1 (and_1_out, R, T1);
  and and_2 (and_2_out, T4, D3);
  and and_3 (and_3_out, T4, D5);
  and and_4 (and_4_out, T6, D6);
  not not_1 (not_1_out, R);
  and and_5 (and_5_out, not_1_out, T1);
  not not_2 (not_2_out, D7);
  and and_6 (and_6_out, not_2_out, I, T3);
  or or_1 (or_1_out, D0, D1, D2, D6);
  or or_2 (store, and_1_out, and_2_out, and_3_out, and_4_out);
  and and_7 (and_7_out, or_1_out, T4);
  or or_3 (load, and_5_out, and_6_out, and_7_out);
endmodule

module ALU (
  input  \and ,
  input  add,
  input  [7:0] INPR,
  input  DR_load,
  input  INPR_load,
  input  [15:0] AC,
  input  [15:0] DR,
  input  complement,
  input  shr,
  input  shl,
  input  E,
  input  load,
  output [15:0] AC_out,
  output E_out
);

  wire alu_1bit_1_c_i_1, alu_1bit_2_c_i_1, alu_1bit_3_c_i_1, alu_1bit_4_c_i_1, alu_1bit_5_c_i_1,
       alu_1bit_6_c_i_1, alu_1bit_7_c_i_1, alu_1bit_8_c_i_1, alu_1bit_9_c_i_1, alu_1bit_10_c_i_1,
       alu_1bit_11_c_i_1, alu_1bit_12_c_i_1, alu_1bit_13_c_i_1, alu_1bit_14_c_i_1, c_7;

  ALU_1bit alu_1bit_1 (
    .INPR_i(INPR[0]), .AC_i_1(AC[1]), .AC_i_1_2(E), .AC_i(AC_out[0]), .DR_i(DR[0]), .c_i(1'b0), .load(load),
    .c_i_1(alu_1bit_1_c_i_1), .\and (\and ), .add(add), .DR_load(DR_load), .inpr(INPR_load),
    .complement(complement), .shr(shr), .shl(shl), .AC_i__in(AC[0]));
  ALU_1bit alu_1bit_2 (
    .INPR_i(1'b0), .AC_i_1(AC[9]), .AC_i_1_2(AC[7]), .AC_i(AC_out[8]), .DR_i(DR[8]), .c_i(c_7), .load(load),
    .c_i_1(alu_1bit_2_c_i_1), .\and (\and ), .add(add), .DR_load(DR_load), .inpr(INPR_load),
    .complement(complement), .shr(shr), .shl(shl), .AC_i__in(AC[8]));
  ALU_1bit alu_1bit_3 (
    .INPR_i(INPR[1]), .AC_i_1(AC[2]), .AC_i_1_2(AC[0]), .AC_i(AC_out[1]), .DR_i(DR[1]),
    .c_i(alu_1bit_1_c_i_1), .load(load), .c_i_1(alu_1bit_3_c_i_1), .\and (\and ), .add(add),
    .DR_load(DR_load), .inpr(INPR_load), .complement(complement), .shr(shr), .shl(shl), .AC_i__in(AC[1]));
  ALU_1bit alu_1bit_4 (
    .INPR_i(1'b0), .AC_i_1(AC[10]), .AC_i_1_2(AC[8]), .AC_i(AC_out[9]), .DR_i(DR[9]), .c_i(alu_1bit_2_c_i_1),
    .load(load), .c_i_1(alu_1bit_4_c_i_1), .\and (\and ), .add(add), .DR_load(DR_load), .inpr(INPR_load),
    .complement(complement), .shr(shr), .shl(shl), .AC_i__in(AC[9]));
  ALU_1bit alu_1bit_5 (
    .INPR_i(INPR[2]), .AC_i_1(AC[3]), .AC_i_1_2(AC[1]), .AC_i(AC_out[2]), .DR_i(DR[2]),
    .c_i(alu_1bit_3_c_i_1), .load(load), .c_i_1(alu_1bit_5_c_i_1), .\and (\and ), .add(add),
    .DR_load(DR_load), .inpr(INPR_load), .complement(complement), .shr(shr), .shl(shl), .AC_i__in(AC[2]));
  ALU_1bit alu_1bit_6 (
    .INPR_i(1'b0), .AC_i_1(AC[11]), .AC_i_1_2(AC[9]), .AC_i(AC_out[10]), .DR_i(DR[10]),
    .c_i(alu_1bit_4_c_i_1), .load(load), .c_i_1(alu_1bit_6_c_i_1), .\and (\and ), .add(add),
    .DR_load(DR_load), .inpr(INPR_load), .complement(complement), .shr(shr), .shl(shl), .AC_i__in(AC[10]));
  ALU_1bit alu_1bit_7 (
    .INPR_i(INPR[3]), .AC_i_1(AC[4]), .AC_i_1_2(AC[2]), .AC_i(AC_out[3]), .DR_i(DR[3]),
    .c_i(alu_1bit_5_c_i_1), .load(load), .c_i_1(alu_1bit_7_c_i_1), .\and (\and ), .add(add),
    .DR_load(DR_load), .inpr(INPR_load), .complement(complement), .shr(shr), .shl(shl), .AC_i__in(AC[3]));
  ALU_1bit alu_1bit_8 (
    .INPR_i(1'b0), .AC_i_1(AC[12]), .AC_i_1_2(AC[10]), .AC_i(AC_out[11]), .DR_i(DR[11]),
    .c_i(alu_1bit_6_c_i_1), .load(load), .c_i_1(alu_1bit_8_c_i_1), .\and (\and ), .add(add),
    .DR_load(DR_load), .inpr(INPR_load), .complement(complement), .shr(shr), .shl(shl), .AC_i__in(AC[11]));
  ALU_1bit alu_1bit_9 (
    .INPR_i(INPR[4]), .AC_i_1(AC[5]), .AC_i_1_2(AC[3]), .AC_i(AC_out[4]), .DR_i(DR[4]),
    .c_i(alu_1bit_7_c_i_1), .load(load), .c_i_1(alu_1bit_9_c_i_1), .\and (\and ), .add(add),
    .DR_load(DR_load), .inpr(INPR_load), .complement(complement), .shr(shr), .shl(shl), .AC_i__in(AC[4]));
  ALU_1bit alu_1bit_10 (
    .INPR_i(1'b0), .AC_i_1(AC[13]), .AC_i_1_2(AC[11]), .AC_i(AC_out[12]), .DR_i(DR[12]),
    .c_i(alu_1bit_8_c_i_1), .load(load), .c_i_1(alu_1bit_10_c_i_1), .\and (\and ), .add(add),
    .DR_load(DR_load), .inpr(INPR_load), .complement(complement), .shr(shr), .shl(shl), .AC_i__in(AC[12]));
  ALU_1bit alu_1bit_11 (
    .INPR_i(INPR[5]), .AC_i_1(AC[6]), .AC_i_1_2(AC[4]), .AC_i(AC_out[5]), .DR_i(DR[5]),
    .c_i(alu_1bit_9_c_i_1), .load(load), .c_i_1(alu_1bit_11_c_i_1), .\and (\and ), .add(add),
    .DR_load(DR_load), .inpr(INPR_load), .complement(complement), .shr(shr), .shl(shl), .AC_i__in(AC[5]));
  ALU_1bit alu_1bit_12 (
    .INPR_i(1'b0), .AC_i_1(AC[14]), .AC_i_1_2(AC[12]), .AC_i(AC_out[13]), .DR_i(DR[13]),
    .c_i(alu_1bit_10_c_i_1), .load(load), .c_i_1(alu_1bit_12_c_i_1), .\and (\and ), .add(add),
    .DR_load(DR_load), .inpr(INPR_load), .complement(complement), .shr(shr), .shl(shl), .AC_i__in(AC[13]));
  ALU_1bit alu_1bit_13 (
    .INPR_i(INPR[6]), .AC_i_1(AC[7]), .AC_i_1_2(AC[5]), .AC_i(AC_out[6]), .DR_i(DR[6]),
    .c_i(alu_1bit_11_c_i_1), .load(load), .c_i_1(alu_1bit_13_c_i_1), .\and (\and ), .add(add),
    .DR_load(DR_load), .inpr(INPR_load), .complement(complement), .shr(shr), .shl(shl), .AC_i__in(AC[6]));
  ALU_1bit alu_1bit_14 (
    .INPR_i(1'b0), .AC_i_1(AC[15]), .AC_i_1_2(AC[13]), .AC_i(AC_out[14]), .DR_i(DR[14]),
    .c_i(alu_1bit_12_c_i_1), .load(load), .c_i_1(alu_1bit_14_c_i_1), .\and (\and ), .add(add),
    .DR_load(DR_load), .inpr(INPR_load), .complement(complement), .shr(shr), .shl(shl), .AC_i__in(AC[14]));
  ALU_1bit alu_1bit_15 (
    .INPR_i(INPR[7]), .AC_i_1(AC[8]), .AC_i_1_2(AC[6]), .AC_i(AC_out[7]), .DR_i(DR[7]),
    .c_i(alu_1bit_13_c_i_1), .load(load), .c_i_1(c_7), .\and (\and ), .add(add), .DR_load(DR_load),
    .inpr(INPR_load), .complement(complement), .shr(shr), .shl(shl), .AC_i__in(AC[7]));
  ALU_1bit alu_1bit_16 (
    .INPR_i(1'b0), .AC_i_1(E), .AC_i_1_2(AC[14]), .AC_i(AC_out[15]), .DR_i(DR[15]), .c_i(alu_1bit_14_c_i_1),
    .load(load), .c_i_1(E_out), .\and (\and ), .add(add), .DR_load(DR_load), .inpr(INPR_load),
    .complement(complement), .shr(shr), .shl(shl), .AC_i__in(AC[15]));

  // Other names for the same wires on the sheet: AC_0 = AC[0]; AC_1 = AC[1]; AC_2 = AC[2]; AC_3 = AC[3]; AC_4 = AC[4];
  //   AC_5 = AC[5]; AC_6 = AC[6]; AC_7 = AC[7]; AC_8 = AC[8]; AC_9 = AC[9]; AC_10 = AC[10]; AC_11 = AC[11];
  //   AC_12 = AC[12]; AC_13 = AC[13]; AC_14 = AC[14]; AC_15 = AC[15]; out_0 = AC_out[0]; out_1 = AC_out[1];
  //   out_2 = AC_out[2]; out_3 = AC_out[3]; out_4 = AC_out[4]; out_5 = AC_out[5]; out_6 = AC_out[6];
  //   out_7 = AC_out[7]; out_8 = AC_out[8]; out_9 = AC_out[9]; out_10 = AC_out[10]; out_11 = AC_out[11];
  //   out_12 = AC_out[12]; out_13 = AC_out[13]; out_14 = AC_out[14]; out_15 = AC_out[15]; comp = complement;
  //   DR_0 = DR[0]; DR_1 = DR[1]; DR_2 = DR[2]; DR_3 = DR[3]; DR_4 = DR[4]; DR_5 = DR[5]; DR_6 = DR[6]; DR_7 = DR[7];
  //   DR_8 = DR[8]; DR_9 = DR[9]; DR_10 = DR[10]; DR_11 = DR[11]; DR_12 = DR[12]; DR_13 = DR[13]; DR_14 = DR[14];
  //   DR_15 = DR[15]; INPR_0 = INPR[0]; INPR_1 = INPR[1]; INPR_2 = INPR[2]; INPR_3 = INPR[3]; INPR_4 = INPR[4];
  //   INPR_5 = INPR[5]; INPR_6 = INPR[6]; INPR_7 = INPR[7]
endmodule

module ALU_1bit (
  input  DR_i,
  input  AC_i__in,
  input  load,
  input  \and ,
  input  c_i,
  input  add,
  input  DR_load,
  input  INPR_i,
  input  inpr,
  input  complement,
  input  AC_i_1,
  input  shr,
  input  AC_i_1_2,
  input  shl,
  output AC_i,
  output c_i_1
);

  wire and_1_out, full_adder_1_sum, not_1_out, not_2_out;

  full_adder full_adder_1 (.a(AC_i__in), .b(DR_i), .c_in(c_i), .sum(full_adder_1_sum), .c_out(c_i_1));
  and and_1 (and_1_out, AC_i__in, DR_i);
  not not_1 (not_1_out, AC_i__in);
  assign AC_i = not_2_out ? AC_i__in : 1'bz;  // Controlled_Buffer controlled_buffer_1
  not not_2 (not_2_out, load);
  assign AC_i = \and  ? and_1_out : 1'bz;  // Controlled_Buffer controlled_buffer_2
  assign AC_i = add ? full_adder_1_sum : 1'bz;  // Controlled_Buffer controlled_buffer_3
  assign AC_i = DR_load ? DR_i : 1'bz;  // Controlled_Buffer controlled_buffer_4
  assign AC_i = inpr ? INPR_i : 1'bz;  // Controlled_Buffer controlled_buffer_5
  assign AC_i = complement ? not_1_out : 1'bz;  // Controlled_Buffer controlled_buffer_6
  assign AC_i = shr ? AC_i_1 : 1'bz;  // Controlled_Buffer controlled_buffer_7
  assign AC_i = shl ? AC_i_1_2 : 1'bz;  // Controlled_Buffer controlled_buffer_8
endmodule

module AC (
  input  [15:0] BUS_in,
  input  increment,
  input  load,
  input  clear,
  input  clock,
  output [15:0] BUS_out
);

  wire or_1_out;
  wire [15:0] multiplexer_1_out, n16_bit_adder_1_sum;

  Multiplexer #(.width(16)) multiplexer_1 (
    .in0(BUS_in), .in1(n16_bit_adder_1_sum), .out(multiplexer_1_out), .sel(increment));  // open: en
  _16_bit_adder u_16_bit_adder_1 (
    .B({16{1'b0}}), .A(BUS_out), .carry_in(1'b1), .SUM(n16_bit_adder_1_sum));  // open: overflow
  or or_1 (or_1_out, increment, load);
  Register #(.width(16)) register_1 (.D(multiplexer_1_out), .en(or_1_out), .Q(BUS_out), .clk(clock), .clr(clear));
endmodule

module AC_control (
  input  r,
  input  p,
  input  T5,
  input  D0,
  input  D1,
  input  D2,
  input  B5,
  input  B6,
  input  B7,
  input  B9,
  input  B11,
  output \and ,
  output add,
  output DR_load,
  output INPR_load,
  output load,
  output complement,
  output shr,
  output shl,
  output increment,
  output clear
);

  and and_1 (\and , T5, D0);
  and and_2 (add, T5, D1);
  and and_3 (DR_load, T5, D2);
  and and_4 (INPR_load, p, B11);
  and and_5 (complement, r, B9);
  and and_6 (shr, r, B7);
  and and_7 (shl, r, B6);
  and and_8 (increment, r, B5);
  and and_9 (clear, r, B11);
  or or_1 (load, \and , add, DR_load, INPR_load, complement, shr, shl);
endmodule

module AR (
  input  [15:0] BUS_input,
  input  inc,
  input  load,
  input  clock,
  input  clear,
  output [11:0] RAM_AR,
  output [15:0] BUS_out
);

  wire or_1_out;
  wire [11:0] multiplexer_1_out, n12_bit_adder_1_sum;

  Multiplexer #(.width(12)) multiplexer_1 (
    .in0(BUS_input[11:0]), .in1(n12_bit_adder_1_sum), .out(multiplexer_1_out), .sel(inc));  // open: en
  _12_bit_adder u_12_bit_adder_1 (
    .B(12'h1), .A(BUS_out[11:0]), .SUM(n12_bit_adder_1_sum), .carry_in(1'b0));  // open: overflow
  or or_1 (or_1_out, inc, load);
  Register #(.width(12)) register_1 (.D(multiplexer_1_out), .en(or_1_out), .Q(BUS_out[11:0]), .clk(clock), .clr(clear));

  assign BUS_out[15:12] = 4'b0000;
  assign RAM_AR = BUS_out[11:0];
endmodule

module AR_control (
  input  I,
  input  R,
  input  T0,
  input  T2,
  input  T3,
  input  T4,
  input  D5,
  input  D7,
  output INCREMNT,
  output LOAD,
  output CLEAR
);

  wire and_1_out, and_2_out, and_3_out, not_1_out, not_2_out, not_3_out, not_4_out;

  not not_1 (not_1_out, R);
  not not_2 (not_2_out, R);
  not not_3 (not_3_out, D7);
  not not_4 (not_4_out, D7);
  and and_1 (and_1_out, not_1_out, T0);
  and and_2 (and_2_out, not_2_out, not_3_out, T2);
  and and_3 (and_3_out, I, T3, not_4_out);
  and and_4 (INCREMNT, T4, D5);
  or or_1 (LOAD, and_1_out, and_2_out, and_3_out);
  and and_5 (CLEAR, R, T0);
endmodule

module DR (
  input  [15:0] BUS_in,
  input  increment,
  input  load,
  input  clear,
  input  clock,
  output [15:0] BUS_out
);

  wire or_1_out;
  wire [15:0] multiplexer_1_out, n16_bit_adder_1_sum;

  Multiplexer #(.width(16)) multiplexer_1 (
    .in0(BUS_in), .in1(n16_bit_adder_1_sum), .out(multiplexer_1_out), .sel(increment));  // open: en
  _16_bit_adder u_16_bit_adder_1 (
    .B(16'h1), .A(BUS_out), .carry_in(1'b0), .SUM(n16_bit_adder_1_sum));  // open: overflow
  or or_1 (or_1_out, increment, load);
  Register #(.width(16)) register_1 (.D(multiplexer_1_out), .en(or_1_out), .Q(BUS_out), .clk(clock), .clr(clear));
endmodule

module DR_control (
  input  T4,
  input  T5,
  input  D0,
  input  D1,
  input  D2,
  input  D6,
  output load,
  output increment
);

  wire or_1_out;

  and and_1 (increment, T5, D6);
  or or_1 (or_1_out, D0, D1, D2, D6);
  and and_2 (load, or_1_out, T4);
endmodule

module PC (
  input  [15:0] BUS_in,
  input  increment,
  input  load,
  input  clear,
  input  clock,
  output [15:0] BUS_out
);

  wire or_1_out;
  wire [15:0] multiplexer_1_out, n16_bit_adder_1_sum;

  Multiplexer #(.width(16)) multiplexer_1 (
    .in0(BUS_in), .in1(n16_bit_adder_1_sum), .out(multiplexer_1_out), .sel(increment));  // open: en
  _16_bit_adder u_16_bit_adder_1 (
    .B(16'h1), .A(BUS_out), .carry_in(1'b0), .SUM(n16_bit_adder_1_sum));  // open: overflow
  or or_1 (or_1_out, increment, load);
  Register #(.width(16)) register_1 (.D(multiplexer_1_out), .en(or_1_out), .Q(BUS_out), .clk(clock), .clr(clear));
endmodule

module PC_control (
  input  [15:0] AC,
  input  [15:0] DR,
  input  R,
  input  r_2,
  input  p,
  input  E,
  input  FGI,
  input  FGO,
  input  T1,
  input  T2,
  input  T4,
  input  T5,
  input  T6,
  input  D4,
  input  D5,
  input  D6,
  input  B1,
  input  B2,
  input  B3,
  input  B4,
  input  B8,
  input  B9,
  output increment,
  output load,
  output clear
);

  wire and_1_out, and_2_out, and_3_out, and_4_out, and_5_out, and_6_out, and_7_out, and_8_out, and_9_out,
       and_10_out, and_11_out, nor_1_out, nor_2_out, not_1_out, not_2_out, not_3_out;

  not not_1 (not_1_out, E);
  nor nor_1 (nor_1_out, AC[0], AC[1], AC[2], AC[3], AC[4], AC[5], AC[6], AC[7], AC[8], AC[9], AC[10], AC[11], AC[12], AC[13], AC[14], AC[15]);
  nor nor_2 (nor_2_out, DR[0], DR[1], DR[2], DR[3], DR[4], DR[5], DR[6], DR[7], DR[8], DR[9], DR[10], DR[11], DR[12], DR[13], DR[14], DR[15]);
  not not_2 (not_2_out, R);
  not not_3 (not_3_out, AC[15]);
  and and_1 (and_1_out, not_2_out, T1);
  and and_2 (and_2_out, R, T2);
  and and_3 (and_3_out, r_2, B4, not_3_out);
  and and_4 (and_4_out, r_2, B3, AC[15]);
  and and_5 (and_5_out, r_2, not_1_out, B1);
  and and_6 (and_6_out, r_2, B2, nor_1_out);
  and and_7 (and_7_out, p, FGI, B9);
  and and_8 (and_8_out, p, FGO, B8);
  and and_9 (and_9_out, T6, D6, nor_2_out);
  and and_10 (and_10_out, T4, D4);
  and and_11 (and_11_out, T5, D5);
  and and_12 (clear, R, T1);
  or or_1 (load, and_10_out, and_11_out);
  or or_2 (increment, and_1_out, and_2_out, and_3_out, and_4_out, and_5_out, and_6_out, and_7_out, and_8_out, and_9_out);
endmodule

module IR (
  input  [15:0] bus_in,
  input  load,
  input  clock,
  output D0,
  output D1,
  output D2,
  output I,
  output D3,
  output D4,
  output D5,
  output D6,
  output D7,
  output [15:0] bus_out,
  output B0,
  output B1,
  output B2,
  output B3,
  output B4,
  output B5,
  output B6,
  output B7,
  output B8,
  output B9,
  output B10,
  output B11
);

  Register #(.width(16)) register_1 (
    .D(bus_in), .en(load), .Q({bus_out[15:12], B11, B10, B9, B8, B7, B6, B5, B4, B3, B2, B1, B0}), .clk(clock));  // open: clr
  Decoder #(.select(3)) decoder_1 (
    .out0(D0), .out1(D1), .out2(D2), .out3(D3), .out4(D4), .out5(D5), .out6(D6), .out7(D7),
    .sel(bus_out[14:12]));  // open: en

  assign bus_out[11:0] = {B11, B10, B9, B8, B7, B6, B5, B4, B3, B2, B1, B0};
  assign I = bus_out[15];
endmodule

module IR_control (
  input  R,
  input  T1,
  output load
);

  wire not_1_out;

  not not_1 (not_1_out, R);
  and and_1 (load, not_1_out, T1);
endmodule

module TR (
  input  load,
  input  clear,
  input  clock,
  output [15:0] BUS_in,
  output [15:0] BUS_out
);

  Register #(.width(16)) register_1 (.D(BUS_in), .en(load), .Q(BUS_out), .clk(clock), .clr(clear));
endmodule

module TR_control (
  input  R,
  input  T0,
  output load
);

  and and_1 (load, R, T0);
endmodule

module OUTR (
  input  [15:0] BUS_in,
  input  load,
  input  clock,
  output [7:0] out
);

  Register register_1 (.D(BUS_in[7:0]), .en(load), .Q(out), .clk(clock));  // open: clr
endmodule

module OUTR_control (
  input  p,
  input  B10,
  output load
);

  and and_1 (load, p, B10);
endmodule

module INPR (
  input  [7:0] \input ,
  input  clock,
  output [7:0] \output 
);

  Register register_1 (.D(\input ), .en(1'b1), .Q(\output ), .clk(clock));  // open: clr
endmodule

module E (
  input  E_input,
  input  complement,
  input  clock,
  input  load,
  input  clear,
  output E_output
);

  wire and_1_out, multiplexer_1_out, or_1_out, undriven;

  Multiplexer multiplexer_1 (.in0(E_input), .in1(complement), .out(multiplexer_1_out), .sel(complement));  // open: en
  and and_1 (and_1_out, multiplexer_1_out, complement);
  J_K_Flip_Flop j_k_ff_1 (
    .J(multiplexer_1_out), .clk(clock), .K(and_1_out), .Q(E_output), .preset(undriven), .en(or_1_out),
    .reset(clear));  // open: Qn
  or or_1 (or_1_out, complement, load);
endmodule

module E_control (
  input  r,
  input  T5,
  input  D1,
  input  B6,
  input  B7,
  input  B8,
  input  B10,
  output load,
  output complement,
  output clear
);

  wire and_1_out, and_2_out, and_3_out;

  and and_1 (and_1_out, T5, D1);
  and and_2 (and_2_out, r, B7);
  and and_3 (and_3_out, r, B6);
  and and_4 (complement, r, B8);
  and and_5 (clear, r, B10);
  or or_1 (load, and_1_out, and_2_out, and_3_out);
endmodule

module R (
  input  T0,
  input  T1,
  input  T2,
  input  FGI,
  input  FGO,
  input  IEN,
  input  clock,
  output R
);

  wire and_1_out, and_2_out, and_3_out, or_1_out;

  and and_1 (and_1_out, ~T0, ~T1, ~T2);  // AND_Gate
  or or_1 (or_1_out, FGI, FGO);
  and and_2 (and_2_out, and_1_out, IEN, or_1_out);
  and and_3 (and_3_out, T2, R);
  J_K_Flip_Flop j_k_ff_1 (.J(and_2_out), .clk(clock), .K(and_3_out), .Q(R));  // open: Qn, preset, en, reset
endmodule

module IEN (
  input  p,
  input  R,
  input  T2,
  input  B6,
  input  B7,
  input  clock,
  output IEN
);

  wire and_1_out, and_2_out, and_3_out, or_1_out;

  and and_1 (and_1_out, p, B6);
  and and_2 (and_2_out, R, T2);
  and and_3 (and_3_out, p, B7);
  or or_1 (or_1_out, and_1_out, and_2_out);
  J_K_Flip_Flop j_k_ff_1 (.J(and_3_out), .clk(clock), .K(or_1_out), .Q(IEN));  // open: Qn, preset, en, reset
endmodule

module FGO (
  input  p,
  input  B10,
  input  T0,
  input  clock,
  output FGO
);

  wire and_1_out;

  and and_1 (and_1_out, B10, p);
  J_K_Flip_Flop j_k_ff_1 (.J(T0), .clk(clock), .K(and_1_out), .Q(FGO));  // open: Qn, preset, en, reset
endmodule

module FGI (
  input  [7:0] INPR,
  input  p,
  input  B11,
  input  clock,
  output FGI
);

  wire and_1_out, or_1_out;

  or or_1 (or_1_out, INPR[7], INPR[6], INPR[5], INPR[4], INPR[3], INPR[2], INPR[1], INPR[0]);
  and and_1 (and_1_out, B11, p);
  J_K_Flip_Flop j_k_ff_1 (.J(or_1_out), .clk(clock), .K(and_1_out), .Q(FGI));  // open: Qn, preset, en, reset
endmodule

module I (
  input  I_in,
  input  R,
  input  T2,
  input  clock,
  output I
);

  wire and_1_out, and_2_out, not_1_out, not_2_out, not_3_out;

  not not_1 (not_1_out, R);
  not not_2 (not_2_out, R);
  not not_3 (not_3_out, I_in);
  and and_1 (and_1_out, T2, not_1_out, I_in);
  and and_2 (and_2_out, T2, not_2_out, not_3_out);
  J_K_Flip_Flop j_k_ff_1 (.J(and_1_out), .clk(clock), .K(and_2_out), .Q(I));  // open: Qn, preset, en, reset
endmodule

module _16_bit_adder (
  input  [15:0] B,
  input  [15:0] A,
  input  carry_in,
  output overflow,
  output [15:0] SUM
);

  wire full_adder_2_c_out, full_adder_3_c_out, full_adder_4_c_out, full_adder_5_c_out, full_adder_6_c_out,
       full_adder_7_c_out, full_adder_8_c_out, full_adder_9_c_out, full_adder_10_c_out, full_adder_11_c_out,
       full_adder_12_c_out, full_adder_13_c_out, full_adder_14_c_out, full_adder_15_c_out,
       full_adder_16_c_out;

  full_adder full_adder_1 (.a(A[15]), .b(B[15]), .c_in(full_adder_2_c_out), .sum(SUM[15]), .c_out(overflow));
  full_adder full_adder_2 (.a(A[14]), .b(B[14]), .c_in(full_adder_3_c_out), .sum(SUM[14]), .c_out(full_adder_2_c_out));
  full_adder full_adder_3 (.a(A[13]), .b(B[13]), .c_in(full_adder_4_c_out), .sum(SUM[13]), .c_out(full_adder_3_c_out));
  full_adder full_adder_4 (.a(A[12]), .b(B[12]), .c_in(full_adder_5_c_out), .sum(SUM[12]), .c_out(full_adder_4_c_out));
  full_adder full_adder_5 (.a(A[11]), .b(B[11]), .c_in(full_adder_6_c_out), .sum(SUM[11]), .c_out(full_adder_5_c_out));
  full_adder full_adder_6 (.a(A[10]), .b(B[10]), .c_in(full_adder_7_c_out), .sum(SUM[10]), .c_out(full_adder_6_c_out));
  full_adder full_adder_7 (.a(A[9]), .b(B[9]), .c_in(full_adder_8_c_out), .sum(SUM[9]), .c_out(full_adder_7_c_out));
  full_adder full_adder_8 (.a(A[8]), .b(B[8]), .c_in(full_adder_9_c_out), .sum(SUM[8]), .c_out(full_adder_8_c_out));
  full_adder full_adder_9 (.a(A[7]), .b(B[7]), .c_in(full_adder_11_c_out), .sum(SUM[7]), .c_out(full_adder_9_c_out));
  full_adder full_adder_10 (.a(A[5]), .b(B[5]), .c_in(full_adder_12_c_out), .sum(SUM[5]), .c_out(full_adder_10_c_out));
  full_adder full_adder_11 (.a(A[6]), .b(B[6]), .c_in(full_adder_10_c_out), .sum(SUM[6]), .c_out(full_adder_11_c_out));
  full_adder full_adder_12 (.a(A[4]), .b(B[4]), .c_in(full_adder_13_c_out), .sum(SUM[4]), .c_out(full_adder_12_c_out));
  full_adder full_adder_13 (.a(A[3]), .b(B[3]), .c_in(full_adder_14_c_out), .sum(SUM[3]), .c_out(full_adder_13_c_out));
  full_adder full_adder_14 (.a(A[2]), .b(B[2]), .c_in(full_adder_15_c_out), .sum(SUM[2]), .c_out(full_adder_14_c_out));
  full_adder full_adder_15 (.a(A[1]), .b(B[1]), .c_in(full_adder_16_c_out), .sum(SUM[1]), .c_out(full_adder_15_c_out));
  full_adder full_adder_16 (.a(A[0]), .b(B[0]), .c_in(carry_in), .sum(SUM[0]), .c_out(full_adder_16_c_out));
endmodule

module _12_bit_adder (
  input  [11:0] B,
  input  [11:0] A,
  input  carry_in,
  output overflow,
  output [11:0] SUM
);

  wire full_adder_2_c_out, full_adder_3_c_out, full_adder_4_c_out, full_adder_5_c_out, full_adder_6_c_out,
       full_adder_7_c_out, full_adder_8_c_out, full_adder_9_c_out, full_adder_10_c_out, full_adder_11_c_out,
       full_adder_12_c_out;

  full_adder full_adder_1 (.a(A[11]), .b(B[11]), .c_in(full_adder_2_c_out), .sum(SUM[11]), .c_out(overflow));
  full_adder full_adder_2 (.a(A[10]), .b(B[10]), .c_in(full_adder_3_c_out), .sum(SUM[10]), .c_out(full_adder_2_c_out));
  full_adder full_adder_3 (.a(A[9]), .b(B[9]), .c_in(full_adder_4_c_out), .sum(SUM[9]), .c_out(full_adder_3_c_out));
  full_adder full_adder_4 (.a(A[8]), .b(B[8]), .c_in(full_adder_5_c_out), .sum(SUM[8]), .c_out(full_adder_4_c_out));
  full_adder full_adder_5 (.a(A[7]), .b(B[7]), .c_in(full_adder_6_c_out), .sum(SUM[7]), .c_out(full_adder_5_c_out));
  full_adder full_adder_6 (.a(A[6]), .b(B[6]), .c_in(full_adder_7_c_out), .sum(SUM[6]), .c_out(full_adder_6_c_out));
  full_adder full_adder_7 (.a(A[5]), .b(B[5]), .c_in(full_adder_8_c_out), .sum(SUM[5]), .c_out(full_adder_7_c_out));
  full_adder full_adder_8 (.a(A[4]), .b(B[4]), .c_in(full_adder_9_c_out), .sum(SUM[4]), .c_out(full_adder_8_c_out));
  full_adder full_adder_9 (.a(A[3]), .b(B[3]), .c_in(full_adder_10_c_out), .sum(SUM[3]), .c_out(full_adder_9_c_out));
  full_adder full_adder_10 (.a(A[2]), .b(B[2]), .c_in(full_adder_11_c_out), .sum(SUM[2]), .c_out(full_adder_10_c_out));
  full_adder full_adder_11 (.a(A[1]), .b(B[1]), .c_in(full_adder_12_c_out), .sum(SUM[1]), .c_out(full_adder_11_c_out));
  full_adder full_adder_12 (.a(A[0]), .b(B[0]), .c_in(carry_in), .sum(SUM[0]), .c_out(full_adder_12_c_out));
endmodule

module full_adder (
  input  a,
  input  b,
  input  c_in,
  output sum,
  output c_out
);

  wire and_1_out, and_2_out, xor_1_out;

  xor xor_1 (xor_1_out, a, b);
  xor xor_2 (sum, xor_1_out, c_in);
  and and_1 (and_1_out, xor_1_out, c_in);
  and and_2 (and_2_out, a, b);
  or or_1 (c_out, and_1_out, and_2_out);
endmodule
